# Fritzing sketch swich_led (saved by Fritzing 0.9.3b)
breadboards: 1

parts:
  R1 = Resistor [tolerance=±5% resistance=330 package=THT]
  S1 = Pushbutton [package="[THT]"]
  Raspberry_Pi_1 = Raspberry Pi 3 [part_number=RPI-3-V1.2]
  LED1 = LED - 5mm [color="Orange (612nm)" package="5 mm [THT]"]
  R2 = Resistor [tolerance=±5% resistance=100 package=THT]

nets:
  N1: R1.Pin_0, Raspberry_Pi_1.GND, LED1.cathode
  N2: R1.Pin_1, S1.Pin_3, S1.Pin_4, Raspberry_Pi_1.GIPO23
  N3: S1.Pin_1, S1.Pin_2
  N4: Raspberry_Pi_1.GIPO21, R2.Pin_0
  N5: LED1.anode, R2.Pin_1
